# Fritzing sketch Hardware_Pinout (saved by Fritzing 0.9.4)
breadboards: 1

parts:
  Heltec_WiFi_LoRa_32_V2 = Heltec WiFi LoRa 32 V2 [part_number=HTIT-WB32LA]
  INMP_441_I²S_Microphone = INMP441
  microSD_Card_Reader = MicroSD Card Module
  Speaker = Piezo Speaker

nets:
  N1: Heltec_WiFi_LoRa_32_V2.pin_2, INMP_441_I²S_Microphone.SD
  N2: Heltec_WiFi_LoRa_32_V2.pin_6, Speaker.pin2
  N3: Heltec_WiFi_LoRa_32_V2.pin_16, Heltec_WiFi_LoRa_32_V2.pin_17, INMP_441_I²S_Microphone.VDD
  GND: Heltec_WiFi_LoRa_32_V2.pin_18, Heltec_WiFi_LoRa_32_V2.pin_19, INMP_441_I²S_Microphone.GND, microSD_Card_Reader.GND, Speaker.pin1
  N4: Heltec_WiFi_LoRa_32_V2.pin_20, microSD_Card_Reader.VCC
  N5: Heltec_WiFi_LoRa_32_V2.pin_21, Heltec_WiFi_LoRa_32_V2.pin_22
  N6: Heltec_WiFi_LoRa_32_V2.pin_28, microSD_Card_Reader.MISO
  N7: Heltec_WiFi_LoRa_32_V2.pin_29, microSD_Card_Reader.MOSI
  N8: Heltec_WiFi_LoRa_32_V2.pin_30, microSD_Card_Reader.SCK
  N9: Heltec_WiFi_LoRa_32_V2.pin_31, microSD_Card_Reader.CS
  N10: Heltec_WiFi_LoRa_32_V2.pin_32, INMP_441_I²S_Microphone.WS
  N11: Heltec_WiFi_LoRa_32_V2.pin_33, INMP_441_I²S_Microphone.SCK

custom parts:
  Heltec WiFi LoRa 32 V2: Heltec WiFi LoRa 32 V2 WiFi LoRa 32 is a classic IoT dev-board designed & produced by Heltec Automation(TM). It’s a highly integrated product based on ESP32 + SX127x, it has Wi-Fi, BLE, LoRa functions, also Li-Po battery management system, 0.96″ OLED are also included. It’s the best choice for smart cities, smart farms, smart home, and IoT makers.
  INMP441: This is a simple breakout board for the INMP441 I2S MEMS microphone.
